# Fritzing sketch Lab04-abde0138 (saved by Fritzing 0.9.10b)
breadboards: 1

parts:
  Teensy1 = Teensy 4.0
  R1 = Resistor [tolerance=±5% power=0.25 resistance=220 package=THT]
  R2 = Resistor [tolerance=±5% power=0.25 resistance=220 package=THT]
  R3 = Resistor [tolerance=±5% power=0.25 resistance=220 package=THT]
  LED1 = RGB LED (com. cathode, rgb) [package="5 mm [THT]"]
  R4 = Resistor [tolerance=±5% power=0.25 resistance=10k package=THT]
  S4 = Pushbutton [package="[THT]"]
  S7 = Pushbutton [package=THT]

nets:
  N1: Teensy1.pin_1, Teensy1.pin_32, LED1.common_cathode, S4.Pin_3, S4.Pin_4, S7.leg1
  N2: Teensy1.pin_6, S7.leg0
  N3: Teensy1.pin_8, R4.Pin_0, S4.Pin_1, S4.Pin_2
  N4: Teensy1.pin_22, R2.Pin_0, R3.Pin_1
  N5: Teensy1.pin_25, R1.Pin_0
  N6: Teensy1.pin_26, R3.Pin_0
  N7: Teensy1.pin_31, R4.Pin_1

notes:
  CST8227 – Interfacing
  Lab 04 – Pushbuttons to Control LED Colors
  Control a tri-color RGB with two switches and a pull-up resistor.
  @author Mostapha Abdelaziz (abde0138)

custom parts:
  Teensy 4.0: The Teensy is a complete USB-based microcontoller development system, in a very small footprint, capable of implementing many types of projects. All programming is done via the USB port. No special programmer is needed, only a standard micro-USB cable and a PC or Macintosh with a USB port.
